# Fritzing sketch ArduinoCarCircuitDiagram (saved by Fritzing 0.9.3b)
breadboards: 1

parts:
  Part1 = Arduino Nano (Rev3.0)
  LED1 = LEDs [package=led10mm]
  LED2 = LEDs [package=led10mm]
  J1 = Piezo Speaker
  HC-SR04_Sensor_1 = HC-SR04 Ultrasonic Distance Sensor
  Part2 = Bluetooth HC-05 Macho
  LED3 = LEDs [package=led10mm]
  LED4 = LEDs [package=led10mm]
  M3 = DC Motor
  VCC1 = Battery block 9V
  U1 = L9110 H-bridge module [part_number="L9110 H-bridge"]
  M4 = DC Motor

nets:
  GND: Part1.GND, LED1.A, LED2.A, J1.pin1, HC-SR04_Sensor_1.GND, Part2.GND, VCC1.-, U1.GND
  VCC: HC-SR04_Sensor_1.VCC, Part2.VCC
  N1: LED3.C, LED4.C
  N2: LED3.A, LED4.A
  N3: M3.pin_2, U1.MOTOR_A-A
  N4: U1.MOTOR_B-A, M4.pin_2
  N5: U1.MOTOR_B-B, M4.pin_1
